// Logisim project Project1_1110_zach_NEW.circ as structural Verilog: 24 circuits, main circuit main
module main (
);

  wire button_1_out, clock_1_out, decoder_1_halt, decoder_1_led, decoder_1_memread, decoder_1_memtoreg,
       decoder_1_memwrite, decoder_1_regwrite, decoder_1_writeled, decoder_1_zerostoalu,
       EX_MEM_mem_memread_2, EX_MEM_mem_memwrite_2, EX_MEM_pcsource, EX_MEM_wb_memtoreg_2,
       EX_MEM_wb_regwrite_2, ID_EX_branch_2, ID_EX_memread_2, ID_EX_memtoreg_2, ID_EX_memwrite_2,
       ID_EX_regwrite_2, MEM_WB_wb_memtoreg_2, MEM_WB_wb_regwrite_2, not_1_out, sixteenbit_alu_1_zero,
       Splitter_subop, Splitter_unsigned;
  wire [1:0] fu_1_muxaen, fu_1_muxben;
  wire [2:0] decoder_1_alusrc, EX_MEM_writeregister_rs_2, ID_EX_ex_ctrl_2, ID_EX_rt_2,
       ID_EX_writeregister_rs_2, MEM_WB_writeregister_2, Splitter_read_register1_rs,
       Splitter_read_register2_rt, Splitter_write_register;
  wire [3:0] decoder_1_opcode_2, ID_EX_opcode_2, Splitter_opcode;
  wire [7:0] adder_1_out, alu_adder_1_adderresult, EX_MEM_adder_result_2, ID_EX_pc_2, IF_ID_pc_out,
       multiplexer_1_out, PC_q, RegtoAddr_address, Splitter_immediate;
  wire [15:0] EX_MEM_readdata2_2, EX_MEM_result_alu_2, ID_EX_imm_ext_2, ID_EX_readdata1_2, ID_EX_readdata2_2,
       IF_ID_output_instruction, MEM_WB_data_2, MEM_WB_result_alu_2, multiplexer_2_out, multiplexer_3_out,
       multiplexer_4_out, multiplexer_5_out, ram_1_data, register_1_q, register_file_1_read_data1,
       register_file_1_read_data2, rom_1_data, sign_extend_1_sign_extended_imm, sixteenbit_alu_1_result;

  Clock clock_1 (.out(clock_1_out));
  not not_1 (not_1_out, decoder_1_halt);
  Register PC (.D(multiplexer_1_out), .en(not_1_out), .Q(PC_q), .clk(clock_1_out), .clr(button_1_out));
  Button button_1 (.out(button_1_out));
  Adder adder_1 (.a(PC_q), .b(8'h1), .out(adder_1_out));  // open: cin, cout
  ROM #(.dataWidth(16)) rom_1 (.addr(PC_q), .data(rom_1_data), .sel(1'b1));
  Multiplexer #(.width(8), .disabled(0), .enable("false")) multiplexer_1 (
    .in0(EX_MEM_adder_result_2), .in1(adder_1_out), .out(multiplexer_1_out), .sel(EX_MEM_pcsource));
  IF_ID_Buffer IF_ID (
    .PC(PC_q), .Input_Instruction(rom_1_data), .Clock(clock_1_out), .PC_out(IF_ID_pc_out),
    .Output_Instruction(IF_ID_output_instruction));
  Instruction_Splitter Splitter (
    .Instruction(IF_ID_output_instruction), .Opcode(Splitter_opcode),
    .Read_Register1_RS(Splitter_read_register1_rs), .Read_Register2_RT(Splitter_read_register2_rt),
    .Write_Register(Splitter_write_register), .SubOp(Splitter_subop), .Unsigned(Splitter_unsigned),
    .Immediate(Splitter_immediate));  // open: Shift_Amount
  Decoder decoder_1 (
    .Opcode(Splitter_opcode), .SubOp(Splitter_subop), .RegWrite(decoder_1_regwrite),
    .Opcode_2(decoder_1_opcode_2), .ALUSrc(decoder_1_alusrc[0]), .MemWrite(decoder_1_memwrite),
    .ZerosToALU(decoder_1_zerostoalu), .MemtoReg(decoder_1_memtoreg), .Halt(decoder_1_halt),
    .LED(decoder_1_led), .WriteLED(decoder_1_writeled), .MemRead(decoder_1_memread));  // open: ShiftSrc, ShifterToReg, RegtoPC, IMMtoPC
  Sign_Extend sign_extend_1 (
    .Unsigned(Splitter_unsigned), .Immediate(Splitter_immediate),
    .Sign_Extended_Imm(sign_extend_1_sign_extended_imm));
  Register_File register_file_1 (
    .Read_Register1(Splitter_read_register1_rs), .Read_Register2(Splitter_read_register2_rt),
    .Write_Register(MEM_WB_writeregister_2), .Write_Data(multiplexer_5_out),
    .Read_Data1(register_file_1_read_data1), .Read_Data2(register_file_1_read_data2),
    .Write_Enable(MEM_WB_wb_regwrite_2), .Clock(clock_1_out));
  ID_EX_Buffer ID_EX (
    .Branch(decoder_1_zerostoalu), .Opcode(decoder_1_opcode_2), .ReadData1(register_file_1_read_data1),
    .ReadData2(register_file_1_read_data2), .IMM_ext(sign_extend_1_sign_extended_imm),
    .EX_CTRL(decoder_1_alusrc), .MemWrite(decoder_1_memwrite), .MemRead(decoder_1_memread),
    .PC(IF_ID_pc_out), .WriteRegister_RS(Splitter_write_register), .MemtoReg(decoder_1_memtoreg),
    .RegWrite(decoder_1_regwrite), .Branch_2(ID_EX_branch_2), .Opcode_2(ID_EX_opcode_2),
    .ReadData1_2(ID_EX_readdata1_2), .ReadData2_2(ID_EX_readdata2_2), .IMM_ext_2(ID_EX_imm_ext_2),
    .EX_CTRL_2(ID_EX_ex_ctrl_2), .MemWrite_2(ID_EX_memwrite_2), .MemRead_2(ID_EX_memread_2),
    .PC_2(ID_EX_pc_2), .WriteRegister_RS_2(ID_EX_writeregister_rs_2), .MemtoReg_2(ID_EX_memtoreg_2),
    .RegWrite_2(ID_EX_regwrite_2), .Clock(clock_1_out), .Rt(Splitter_read_register2_rt), .Rt_2(ID_EX_rt_2));  // open: SubOp, Shamt, SubOp_2, Shamt_2, Bubble
  Multiplexer #(.select(2), .width(16), .disabled(0), .enable("false")) multiplexer_2 (
    .in0(ID_EX_readdata1_2), .in1(multiplexer_5_out), .in2(EX_MEM_result_alu_2), .out(multiplexer_2_out),
    .sel(fu_1_muxaen));  // open: in3
  Multiplexer #(.select(2), .width(16), .disabled(0), .enable("false")) multiplexer_3 (
    .in0(ID_EX_readdata2_2), .in1(multiplexer_5_out), .in2(EX_MEM_result_alu_2), .out(multiplexer_3_out),
    .sel(fu_1_muxben));  // open: in3
  Multiplexer #(.width(16), .disabled(0), .enable("false")) multiplexer_4 (
    .in0(multiplexer_3_out), .in1(ID_EX_imm_ext_2), .out(multiplexer_4_out), .sel(ID_EX_ex_ctrl_2[0]));
  ALU_Adder alu_adder_1 (.PC(ID_EX_pc_2), .IMM_ext(ID_EX_readdata2_2), .AdderResult(alu_adder_1_adderresult));
  FU fu_1 (
    .MuxAEn(fu_1_muxaen), .MuxBEn(fu_1_muxben), .RS_EX(ID_EX_writeregister_rs_2),
    .RS_Mem(EX_MEM_writeregister_rs_2), .RegisterWrite_Mem(EX_MEM_wb_regwrite_2),
    .RS_WB(MEM_WB_writeregister_2), .RegisterWrite_WB(MEM_WB_wb_regwrite_2), .RT_EX(ID_EX_rt_2));
  sixteenBit_ALU sixteenbit_alu_1 (
    .ALUOperation(ID_EX_opcode_2), .a(multiplexer_2_out), .Zero(sixteenbit_alu_1_zero),
    .Result(sixteenbit_alu_1_result), .b(multiplexer_4_out));  // open: Overflow
  EX_MEM_Buffer EX_MEM (
    .MEM_MemWrite(ID_EX_memwrite_2), .MEM_MemRead(ID_EX_memread_2), .MEM_Branch(ID_EX_branch_2),
    .WB_MemtoReg(ID_EX_memtoreg_2), .WB_RegWrite(ID_EX_regwrite_2), .Adder_Result(alu_adder_1_adderresult),
    .Zero_ALU(sixteenbit_alu_1_zero), .Result_ALU(sixteenbit_alu_1_result), .ReadData2(ID_EX_readdata2_2),
    .WriteRegister_RS(ID_EX_writeregister_rs_2), .Clock(clock_1_out), .MEM_MemWrite_2(EX_MEM_mem_memwrite_2),
    .MEM_MemRead_2(EX_MEM_mem_memread_2), .WB_MemtoReg_2(EX_MEM_wb_memtoreg_2),
    .WB_RegWrite_2(EX_MEM_wb_regwrite_2), .Adder_Result_2(EX_MEM_adder_result_2), .PCSource(EX_MEM_pcsource),
    .Result_ALU_2(EX_MEM_result_alu_2), .ReadData2_2(EX_MEM_readdata2_2),
    .WriteRegister_RS_2(EX_MEM_writeregister_rs_2));  // open: Bubble
  ALUtoPC RegtoAddr (.ALUOut(EX_MEM_result_alu_2), .Address(RegtoAddr_address));
  Register #(.width(16)) register_1 (
    .D(EX_MEM_readdata2_2), .en(decoder_1_writeled), .Q(register_1_q), .clk(clock_1_out));  // open: clr
  RAM #(.dataWidth(16), .bus("separate")) ram_1 (
    .addr(RegtoAddr_address), .din(EX_MEM_readdata2_2), .data(ram_1_data), .str(EX_MEM_mem_memwrite_2),
    .sel(1'b1), .clk(clock_1_out), .ld(EX_MEM_mem_memread_2));  // open: clr
  Hex_Digit_Display hex_digit_display_1 (.value(register_1_q[15:12]));  // open: dp
  LED Halt (.in(decoder_1_led));
  Hex_Digit_Display hex_digit_display_2 (.value(register_1_q[11:8]));  // open: dp
  Hex_Digit_Display hex_digit_display_3 (.value(register_1_q[7:4]));  // open: dp
  Mem_WB_Buffer MEM_WB (
    .WB_MemtoReg(EX_MEM_wb_memtoreg_2), .WB_RegWrite(EX_MEM_wb_regwrite_2), .Data(ram_1_data),
    .Result_ALU(EX_MEM_result_alu_2), .WriteRegister(EX_MEM_writeregister_rs_2), .Clock(clock_1_out),
    .WB_MemtoReg_2(MEM_WB_wb_memtoreg_2), .WB_RegWrite_2(MEM_WB_wb_regwrite_2), .Data_2(MEM_WB_data_2),
    .Result_ALU_2(MEM_WB_result_alu_2), .WriteRegister_2(MEM_WB_writeregister_2));  // open: Bubble
  Hex_Digit_Display hex_digit_display_4 (.value(register_1_q[3:0]));  // open: dp
  Multiplexer #(.width(16), .disabled(0), .enable("false")) multiplexer_5 (
    .in0(MEM_WB_data_2), .in1(MEM_WB_result_alu_2), .out(multiplexer_5_out), .sel(MEM_WB_wb_memtoreg_2));

  // Notes on the sheet:
  //   contents of rom_1 (hex, n*v repeats v):
  //   4*0 1204 1403 0 0 0 1403
endmodule

module Instruction_Splitter (
  input  [15:0] Instruction,
  output [3:0] Opcode,
  output [2:0] Read_Register1_RS,
  output [2:0] Read_Register2_RT,
  output [2:0] Write_Register,
  output [3:0] Shift_Amount,
  output SubOp,
  output Unsigned,
  output [7:0] Immediate
);


  assign Immediate = Instruction[7:0];
  assign Opcode = Instruction[15:12];
  assign Read_Register1_RS = Instruction[11:9];
  assign Read_Register2_RT = Instruction[8:6];
  assign Shift_Amount = Instruction[4:1];
  assign SubOp = Instruction[0];
  assign Unsigned = Instruction[8];
  assign Write_Register = Instruction[11:9];
endmodule

module Sign_Extend (
  input  Unsigned,
  input  [7:0] Immediate,
  output [15:0] Sign_Extended_Imm
);

  wire [15:0] bit_extender_1_out, bit_extender_2_out;

  assign bit_extender_1_out = {{8{Immediate[7]}}, Immediate};  // Bit_Extender bit_extender_1
  assign bit_extender_2_out = {{8{1'b0}}, Immediate};  // Bit_Extender bit_extender_2
  Multiplexer #(.width(16), .disabled(0), .enable("false")) multiplexer_1 (
    .in0(bit_extender_1_out), .in1(bit_extender_2_out), .out(Sign_Extended_Imm), .sel(Unsigned));
endmodule

// RegisterFile
module Register_File (
  input  [2:0] Read_Register1,
  input  [2:0] Read_Register2,
  input  [2:0] Write_Register,
  input  [15:0] Write_Data,
  input  Write_Enable,
  input  Clock,
  output [15:0] Read_Data1,
  output [15:0] Read_Data2
);

  wire decoder_1_out0, decoder_1_out1, decoder_1_out2, decoder_1_out3, decoder_1_out4, decoder_1_out5,
       decoder_1_out6, decoder_1_out7;
  wire [15:0] R0_q, R1_q, R2_q, R3_q, R4_q, R5_q, R6_q, R7_q;

  Decoder_part #(.select(3), .disabled(0)) decoder_1 (
    .out0(decoder_1_out0), .out1(decoder_1_out1), .out2(decoder_1_out2), .out3(decoder_1_out3),
    .out4(decoder_1_out4), .out5(decoder_1_out5), .out6(decoder_1_out6), .out7(decoder_1_out7),
    .sel(Write_Register), .en(Write_Enable));
  Register #(.width(16)) R0 (.D(Write_Data), .en(decoder_1_out0), .Q(R0_q), .clk(Clock));  // open: clr
  Register #(.width(16)) R1 (.D(Write_Data), .en(decoder_1_out1), .Q(R1_q), .clk(Clock));  // open: clr
  Register #(.width(16)) R2 (.D(Write_Data), .en(decoder_1_out2), .Q(R2_q), .clk(Clock));  // open: clr
  Register #(.width(16)) R3 (.D(Write_Data), .en(decoder_1_out3), .Q(R3_q), .clk(Clock));  // open: clr
  Register #(.width(16)) R4 (.D(Write_Data), .en(decoder_1_out4), .Q(R4_q), .clk(Clock));  // open: clr
  Register #(.width(16)) R5 (.D(Write_Data), .en(decoder_1_out5), .Q(R5_q), .clk(Clock));  // open: clr
  Register #(.width(16)) R6 (.D(Write_Data), .en(decoder_1_out6), .Q(R6_q), .clk(Clock));  // open: clr
  Register #(.width(16)) R7 (.D(Write_Data), .en(decoder_1_out7), .Q(R7_q), .clk(Clock));  // open: clr
  Multiplexer #(.select(3), .width(16), .enable("false")) multiplexer_1 (
    .in0(R0_q), .in1(R1_q), .in2(R2_q), .in3(R3_q), .in4(R4_q), .in5(R5_q), .in6(R6_q), .in7(R7_q),
    .out(Read_Data1), .sel(Read_Register1));
  Multiplexer #(.select(3), .width(16), .enable("false")) multiplexer_2 (
    .in0(R0_q), .in1(R1_q), .in2(R2_q), .in3(R3_q), .in4(R4_q), .in5(R5_q), .in6(R6_q), .in7(R7_q),
    .out(Read_Data2), .sel(Read_Register2));
endmodule

module ALUtoPC (
  input  [15:0] ALUOut,
  output [7:0] Address
);


  assign Address = ALUOut[7:0];
endmodule

module sixteenBit_ALU (
  input  [3:0] ALUOperation,
  input  [15:0] a,
  input  [15:0] b,
  output Zero,
  output [15:0] Result,
  output Overflow
);

  wire one_bit_alu_1_p3, one_bit_alu_1_p6, one_bit_alu_2_p6, one_bit_alu_3_p6, one_bit_alu_4_p6,
       one_bit_alu_5_p6, one_bit_alu_6_p6, one_bit_alu_7_p6, one_bit_alu_8_p6, one_bit_alu_9_p6,
       one_bit_alu_10_p6, one_bit_alu_11_p6, one_bit_alu_12_p6, one_bit_alu_13_p6, one_bit_alu_14_p6,
       one_bit_alu_15_p6, one_bit_alu_16_p6, one_bit_alu_16_p10;

  // reference_circuit_one_bit_ALU one_bit_alu_1: pin names not known; wires that end beside it: a[0], b[0], one_bit_alu_1_p3, ALUOperation[3], ALUOperation[2], one_bit_alu_1_p6, ALUOperation[2], ALUOperation[1:0], Result[0]
  // reference_circuit_one_bit_ALU one_bit_alu_2: pin names not known; wires that end beside it: a[1], b[1], 1'b0, ALUOperation[3], ALUOperation[2], one_bit_alu_2_p6, one_bit_alu_1_p6, ALUOperation[1:0], Result[1]
  // reference_circuit_one_bit_ALU one_bit_alu_3: pin names not known; wires that end beside it: a[2], b[2], 1'b0, ALUOperation[3], ALUOperation[2], one_bit_alu_3_p6, one_bit_alu_2_p6, ALUOperation[1:0], Result[2]
  // reference_circuit_one_bit_ALU one_bit_alu_4: pin names not known; wires that end beside it: a[3], b[3], 1'b0, ALUOperation[3], ALUOperation[2], one_bit_alu_4_p6, one_bit_alu_3_p6, ALUOperation[1:0], Result[3]
  // reference_circuit_one_bit_ALU one_bit_alu_5: pin names not known; wires that end beside it: a[4], b[4], 1'b0, ALUOperation[3], ALUOperation[2], one_bit_alu_5_p6, one_bit_alu_4_p6, ALUOperation[1:0], Result[4]
  // reference_circuit_one_bit_ALU one_bit_alu_6: pin names not known; wires that end beside it: a[5], b[5], 1'b0, ALUOperation[3], ALUOperation[2], one_bit_alu_6_p6, one_bit_alu_5_p6, ALUOperation[1:0], Result[5]
  // reference_circuit_one_bit_ALU one_bit_alu_7: pin names not known; wires that end beside it: a[6], b[6], 1'b0, ALUOperation[3], ALUOperation[2], one_bit_alu_7_p6, one_bit_alu_6_p6, ALUOperation[1:0], Result[6]
  // reference_circuit_one_bit_ALU one_bit_alu_8: pin names not known; wires that end beside it: a[7], b[7], 1'b0, ALUOperation[3], ALUOperation[2], one_bit_alu_8_p6, one_bit_alu_7_p6, ALUOperation[1:0], Result[7]
  // reference_circuit_one_bit_ALU one_bit_alu_9: pin names not known; wires that end beside it: a[8], b[8], 1'b0, ALUOperation[3], ALUOperation[2], one_bit_alu_9_p6, one_bit_alu_8_p6, ALUOperation[1:0], Result[8]
  // reference_circuit_one_bit_ALU one_bit_alu_10: pin names not known; wires that end beside it: a[9], b[9], 1'b0, ALUOperation[3], ALUOperation[2], one_bit_alu_10_p6, one_bit_alu_9_p6, ALUOperation[1:0], Result[9]
  // reference_circuit_one_bit_ALU one_bit_alu_11: pin names not known; wires that end beside it: a[10], b[10], 1'b0, ALUOperation[3], ALUOperation[2], one_bit_alu_11_p6, one_bit_alu_10_p6, ALUOperation[1:0], Result[10]
  // reference_circuit_one_bit_ALU one_bit_alu_12: pin names not known; wires that end beside it: a[11], b[11], 1'b0, ALUOperation[3], ALUOperation[2], one_bit_alu_12_p6, one_bit_alu_11_p6, ALUOperation[1:0], Result[11]
  // reference_circuit_one_bit_ALU one_bit_alu_13: pin names not known; wires that end beside it: a[12], b[12], 1'b0, ALUOperation[3], ALUOperation[2], one_bit_alu_13_p6, one_bit_alu_12_p6, ALUOperation[1:0], Result[12]
  // reference_circuit_one_bit_ALU one_bit_alu_14: pin names not known; wires that end beside it: a[13], b[13], 1'b0, ALUOperation[3], ALUOperation[2], one_bit_alu_14_p6, one_bit_alu_13_p6, ALUOperation[1:0], Result[13]
  // reference_circuit_one_bit_ALU one_bit_alu_15: pin names not known; wires that end beside it: a[14], b[14], 1'b0, ALUOperation[3], ALUOperation[2], one_bit_alu_15_p6, one_bit_alu_14_p6, ALUOperation[1:0], Result[14]
  // reference_circuit_one_bit_ALU one_bit_alu_16: pin names not known; wires that end beside it: a[15], b[15], 1'b0, ALUOperation[3], ALUOperation[2], one_bit_alu_16_p6, one_bit_alu_15_p6, ALUOperation[1:0], Result[15], one_bit_alu_16_p10
  xor xor_1 (one_bit_alu_1_p3, one_bit_alu_16_p10, Overflow);
  xor xor_2 (Overflow, one_bit_alu_15_p6, one_bit_alu_16_p6);
  nor nor_1 (Zero, Result[0], Result[1], Result[2], Result[3], Result[4], Result[5], Result[6], Result[7], Result[8], Result[9], Result[10], Result[11], Result[12], Result[13], Result[14], Result[15]);
endmodule

module one_bit_ALU (
  input  CarryIn,
  input  [1:0] Operation,
  input  Ainvert,
  input  Binvert,
  input  a,
  input  b,
  input  Less,
  output Result,
  output Set,
  output CarryOut
);

  wire and_1_out, multiplexer_1_out, multiplexer_2_out, not_1_out, not_2_out, or_1_out;

  not not_1 (not_1_out, a);
  Multiplexer #(.enable("false")) multiplexer_1 (.in0(a), .in1(not_1_out), .out(multiplexer_1_out), .sel(Ainvert));
  Multiplexer #(.enable("false")) multiplexer_2 (.in0(b), .in1(not_2_out), .out(multiplexer_2_out), .sel(Binvert));
  not not_2 (not_2_out, b);
  and and_1 (and_1_out, multiplexer_1_out, multiplexer_2_out);
  or or_1 (or_1_out, multiplexer_1_out, multiplexer_2_out);
  Adder #(.width(1)) adder_1 (.a(multiplexer_1_out), .b(multiplexer_2_out), .out(Set), .cin(CarryIn), .cout(CarryOut));
  Multiplexer #(.select(2), .enable("false")) multiplexer_3 (
    .in0(and_1_out), .in1(or_1_out), .in2(Set), .in3(Less), .out(Result), .sel(Operation));
endmodule

module ResultToLess (
  input  [15:0] Result,
  output Less
);


  assign Less = Result[15];
endmodule

module Decoder (
  input  [3:0] Opcode,
  input  SubOp,
  output ShiftSrc,
  output ShifterToReg,
  output RegWrite,
  output [3:0] Opcode_2,
  output ALUSrc,
  output RegtoPC,
  output IMMtoPC,
  output MemWrite,
  output ZerosToALU,
  output MemtoReg,
  output Halt,
  output LED,
  output WriteLED,
  output MemRead
);

  wire Arith_Log_Decoder_regwrite, MemDecoder_regwrite, ShifterDecoder_regwrite;
  wire [3:0] Arith_Log_Decoder_aluoperation, PCDecoder_aluop;

  ShifterDecoder ShifterDecoder (
    .Opcode(Opcode), .ShiftSrc(ShiftSrc), .ShifterToReg(ShifterToReg), .RegWrite(ShifterDecoder_regwrite));
  Arith_Log_Decoder Arith_Log_Decoder (
    .Opcode(Opcode), .SubOp(SubOp), .ALUOperation(Arith_Log_Decoder_aluoperation),
    .RegWrite(Arith_Log_Decoder_regwrite), .ALUsrc(ALUSrc));
  PCDecoder PCDecoder (
    .Opcode(Opcode), .Subop(SubOp), .RegtoPC(RegtoPC), .IMMtoPC(IMMtoPC), .ZerosToALU(ZerosToALU),
    .ALUOp(PCDecoder_aluop));
  MemDecoder MemDecoder (
    .Opcode(Opcode), .Subop(SubOp), .MemWrite(MemWrite), .MemtoReg(MemtoReg), .RegWrite(MemDecoder_regwrite),
    .MemRead(MemRead));
  HaltDecoder HaltDecoder (.Opcode(Opcode), .Halt(Halt), .LED(LED));
  PutDecoder PutDecoder (.Opcode(Opcode), .WriteLED(WriteLED));
  or or_1 (RegWrite, Arith_Log_Decoder_regwrite, ShifterDecoder_regwrite, MemDecoder_regwrite);
  assign Opcode_2 = Arith_Log_Decoder_aluoperation | PCDecoder_aluop;  // OR_Gate or_2, 4 bits wide
endmodule

module ShifterDecoder (
  input  [3:0] Opcode,
  output ShiftSrc,
  output ShifterToReg,
  output RegWrite
);

  wire not_1_out, not_2_out;

  not not_1 (not_1_out, Opcode[3]);
  not not_2 (not_2_out, Opcode[1]);
  and and_1 (RegWrite, not_1_out, Opcode[2], not_2_out);

  assign ShifterToReg = RegWrite;
  assign ShiftSrc = Opcode[0];
endmodule

module Arith_Log_Decoder (
  input  [3:0] Opcode,
  input  SubOp,
  output [3:0] ALUOperation,
  output RegWrite,
  output ALUsrc
);

  wire and_2_out, and_3_out, and_5_out, and_6_out, not_1_out, not_2_out, not_3_out, not_4_out, not_5_out,
       not_6_out, not_7_out, not_8_out, not_9_out, not_10_out, not_11_out, not_12_out, not_13_out,
       not_14_out, not_15_out, not_16_out, not_17_out, not_18_out, not_19_out, not_20_out, not_21_out;

  not not_1 (not_1_out, Opcode[3]);
  not not_2 (not_2_out, Opcode[2]);
  not not_3 (not_3_out, SubOp);
  and and_1 (ALUOperation[3], not_1_out, not_2_out, Opcode[1], Opcode[0], not_3_out);
  not not_4 (not_4_out, Opcode[3]);
  not not_5 (not_5_out, Opcode[2]);
  and and_2 (and_2_out, not_4_out, not_5_out, not_6_out, not_7_out, SubOp);
  not not_6 (not_6_out, Opcode[1]);
  not not_7 (not_7_out, Opcode[0]);
  not not_8 (not_8_out, Opcode[3]);
  not not_9 (not_9_out, Opcode[2]);
  and and_3 (and_3_out, not_8_out, not_9_out, Opcode[1], Opcode[0], not_10_out);
  not not_10 (not_10_out, SubOp);
  not not_11 (not_11_out, Opcode[3]);
  and and_4 (ALUOperation[1], not_11_out, not_12_out, not_13_out);
  not not_12 (not_12_out, Opcode[2]);
  not not_13 (not_13_out, Opcode[1]);
  not not_14 (not_14_out, Opcode[3]);
  and and_5 (and_5_out, not_14_out, not_15_out, not_16_out);
  not not_15 (not_15_out, Opcode[2]);
  not not_16 (not_16_out, Opcode[1]);
  not not_17 (not_17_out, Opcode[3]);
  and and_6 (and_6_out, not_17_out, not_18_out, Opcode[0]);
  not not_18 (not_18_out, Opcode[2]);
  not not_19 (not_19_out, Opcode[3]);
  not not_20 (not_20_out, Opcode[2]);
  and and_7 (ALUsrc, not_19_out, not_20_out, not_21_out, Opcode[0]);
  not not_21 (not_21_out, Opcode[1]);
  or or_1 (RegWrite, and_5_out, and_6_out);
  or or_2 (ALUOperation[2], and_2_out, and_3_out);

  assign ALUOperation[0] = 1'b0;
endmodule

module PCDecoder (
  input  [3:0] Opcode,
  input  Subop,
  output RegtoPC,
  output IMMtoPC,
  output ZerosToALU,
  output [3:0] ALUOp
);

  wire and_2_out, and_3_out, and_4_out, and_5_out, and_8_out, not_1_out, not_2_out, not_3_out, not_4_out,
       not_5_out, not_6_out, not_7_out, not_8_out, not_9_out, not_10_out, not_11_out, not_12_out;

  not not_1 (not_1_out, Opcode[1]);
  not not_2 (not_2_out, Subop);
  not not_3 (not_3_out, Opcode[2]);
  not not_4 (not_4_out, Opcode[1]);
  not not_5 (not_5_out, Opcode[0]);
  not not_6 (not_6_out, Opcode[2]);
  not not_7 (not_7_out, Opcode[1]);
  not not_8 (not_8_out, Opcode[2]);
  not not_9 (not_9_out, Opcode[0]);
  not not_10 (not_10_out, Opcode[0]);
  not not_11 (not_11_out, Opcode[2]);
  not not_12 (not_12_out, Opcode[2]);
  and and_1 (RegtoPC, Opcode[3], Opcode[2], not_1_out, Opcode[0], not_2_out);
  and and_2 (and_2_out, Opcode[3], not_6_out, Opcode[0], not_7_out);
  and and_3 (and_3_out, Opcode[3], not_8_out, Opcode[0]);
  and and_4 (and_4_out, Opcode[3], Opcode[1], not_9_out);
  and and_5 (and_5_out, Opcode[3], Opcode[2], Opcode[1], not_10_out);
  and and_6 (ZerosToALU, Opcode[3], not_11_out);
  and and_7 (ALUOp[1], Opcode[3], not_12_out);
  and and_8 (and_8_out, Opcode[3], not_3_out, not_4_out, not_5_out);
  or or_1 (IMMtoPC, and_8_out, and_2_out, and_3_out, and_4_out, and_5_out);

  assign {ALUOp[3:2], ALUOp[0]} = 3'b000;
endmodule

module MemDecoder (
  input  [3:0] Opcode,
  input  Subop,
  output MemWrite,
  output MemtoReg,
  output RegWrite,
  output MemRead
);

  wire not_1_out, not_2_out, not_3_out, not_4_out, not_5_out;

  not not_1 (not_1_out, Opcode[0]);
  and and_1 (MemWrite, not_1_out, Opcode[1], Opcode[2], not_2_out, Subop);
  not not_2 (not_2_out, Opcode[3]);
  not not_3 (not_3_out, Opcode[0]);
  and and_2 (MemRead, not_3_out, Opcode[1], Opcode[2], not_4_out, not_5_out);
  not not_4 (not_4_out, Opcode[3]);
  not not_5 (not_5_out, Subop);

  assign MemtoReg = MemRead;
  assign RegWrite = MemRead;
endmodule

module HaltDecoder (
  input  [3:0] Opcode,
  output Halt,
  output LED
);

  wire not_1_out;

  not not_1 (not_1_out, Opcode[3]);
  and and_1 (Halt, Opcode[0], Opcode[1], Opcode[2], not_1_out);

  assign LED = Halt;
endmodule

module PutDecoder (
  input  [3:0] Opcode,
  output WriteLED
);

  and and_1 (WriteLED, Opcode[0], Opcode[1], Opcode[2], Opcode[3]);
endmodule

module JALDecoder (
  input  [3:0] Opcode,
  output IMMtoPC,
  output PCtoReg,
  output RegWrite
);

  wire not_1_out, not_2_out;

  not not_1 (not_1_out, Opcode[0]);
  not not_2 (not_2_out, Opcode[1]);
  and and_1 (IMMtoPC, not_1_out, not_2_out, Opcode[2], Opcode[3]);

  assign PCtoReg = IMMtoPC;
  assign RegWrite = IMMtoPC;
endmodule

module Shifter (
  input  Subop,
  input  [15:0] Data,
  input  [15:0] ShamtReg,
  input  ShiftSrc,
  input  [3:0] Shamt,
  output [15:0] ShiftOut
);

  wire [3:0] multiplexer_1_out;
  wire [15:0] shifter_1_out, shifter_2_out;

  Multiplexer #(.width(4), .disabled(0), .enable("false")) multiplexer_1 (
    .in0(ShamtReg[3:0]), .in1(Shamt), .out(multiplexer_1_out), .sel(ShiftSrc));
  Shifter_part #(.width(16)) shifter_1 (.in(Data), .\dist (multiplexer_1_out), .out(shifter_1_out));
  Shifter_part #(.width(16), .shift("lr")) shifter_2 (.in(Data), .\dist (multiplexer_1_out), .out(shifter_2_out));
  Multiplexer #(.width(16), .disabled(0), .enable("false")) multiplexer_2 (
    .in0(shifter_1_out), .in1(shifter_2_out), .out(ShiftOut), .sel(Subop));
endmodule

module IF_ID_Buffer (
  input  [7:0] PC,
  input  [15:0] Input_Instruction,
  input  Clock,
  output [7:0] PC_out,
  output [15:0] Output_Instruction
);

  Register #(.trigger("falling")) register_1 (.D(PC), .Q(PC_out), .clk(Clock));  // open: en, clr
  Register #(.width(16), .trigger("falling")) register_2 (
    .D(Input_Instruction), .Q(Output_Instruction), .clk(Clock));  // open: en, clr
endmodule

module ID_EX_Buffer (
  input  Branch,
  input  [3:0] Opcode,
  input  SubOp,
  input  [15:0] ReadData1,
  input  [3:0] Shamt,
  input  [15:0] ReadData2,
  input  [15:0] IMM_ext,
  input  [2:0] EX_CTRL,
  input  MemWrite,
  input  MemRead,
  input  [7:0] PC,
  input  [2:0] WriteRegister_RS,
  input  MemtoReg,
  input  RegWrite,
  input  [2:0] Rt,
  input  Bubble,
  input  Clock,
  output Branch_2,
  output [3:0] Opcode_2,
  output SubOp_2,
  output [15:0] ReadData1_2,
  output [3:0] Shamt_2,
  output [15:0] ReadData2_2,
  output [15:0] IMM_ext_2,
  output [2:0] EX_CTRL_2,
  output MemWrite_2,
  output MemRead_2,
  output [7:0] PC_2,
  output [2:0] WriteRegister_RS_2,
  output MemtoReg_2,
  output RegWrite_2,
  output [2:0] Rt_2
);

  wire and_1_out, and_3_out, and_4_out, and_5_out;
  wire [2:0] and_2_out;
  wire [2:2] not_1_out;

  not not_1 (not_1_out[2], 1'b0);
  and and_1 (and_1_out, Branch, not_1_out[2]);
  assign and_2_out = EX_CTRL & {3{not_1_out[2]}};  // AND_Gate and_2, 3 bits wide
  and and_3 (and_3_out, MemWrite, not_1_out[2]);
  and and_4 (and_4_out, MemtoReg, not_1_out[2]);
  and and_5 (and_5_out, RegWrite, not_1_out[2]);
  Register #(.width(1), .trigger("falling")) register_1 (.D(and_1_out), .Q(Branch_2), .clk(Clock));  // open: en, clr
  Register #(.width(4), .trigger("falling")) register_2 (.D(Opcode), .Q(Opcode_2), .clk(Clock));  // open: en, clr
  Register #(.width(1), .trigger("falling")) register_3 (.D(SubOp), .Q(SubOp_2), .clk(Clock));  // open: en, clr
  Register #(.width(16), .trigger("falling")) register_4 (
    .D(ReadData1), .Q(ReadData1_2), .clk(Clock));  // open: en, clr
  Register #(.width(4), .trigger("falling")) register_5 (.D(Shamt), .Q(Shamt_2), .clk(Clock));  // open: en, clr
  Register #(.width(16), .trigger("falling")) register_6 (
    .D(ReadData2), .Q(ReadData2_2), .clk(Clock));  // open: en, clr
  Register #(.width(16), .trigger("falling")) register_7 (.D(IMM_ext), .Q(IMM_ext_2), .clk(Clock));  // open: en, clr
  Register #(.width(3), .trigger("falling")) register_8 (.D(and_2_out), .Q(EX_CTRL_2), .clk(Clock));  // open: en, clr
  Register #(.width(1), .trigger("falling")) register_9 (.D(and_3_out), .Q(MemWrite_2), .clk(Clock));  // open: en, clr
  Register #(.width(1), .trigger("falling")) register_10 (.D(MemRead), .Q(MemRead_2), .clk(Clock));  // open: en, clr
  Register #(.trigger("falling")) register_11 (.D(PC), .Q(PC_2), .clk(Clock));  // open: en, clr
  Register #(.width(3), .trigger("falling")) register_12 (
    .D(WriteRegister_RS), .Q(WriteRegister_RS_2), .clk(Clock));  // open: en, clr
  Register #(.width(1), .trigger("falling")) register_13 (.D(and_4_out), .Q(MemtoReg_2), .clk(Clock));  // open: en, clr
  Register #(.width(1)) register_14 (.D(and_5_out), .Q(RegWrite_2), .clk(Clock));  // open: en, clr
  Register #(.width(3), .trigger("falling")) register_15 (.D(Rt), .Q(Rt_2), .clk(Clock));  // open: en, clr
endmodule

module EX_MEM_Buffer (
  input  MEM_MemWrite,
  input  MEM_MemRead,
  input  MEM_Branch,
  input  WB_MemtoReg,
  input  WB_RegWrite,
  input  [7:0] Adder_Result,
  input  Zero_ALU,
  input  [15:0] Result_ALU,
  input  [15:0] ReadData2,
  input  [2:0] WriteRegister_RS,
  input  Bubble,
  input  Clock,
  output MEM_MemWrite_2,
  output MEM_MemRead_2,
  output WB_MemtoReg_2,
  output WB_RegWrite_2,
  output [7:0] Adder_Result_2,
  output PCSource,
  output [15:0] Result_ALU_2,
  output [15:0] ReadData2_2,
  output [2:0] WriteRegister_RS_2
);

  wire and_1_out, and_2_out, and_3_out, and_4_out, and_5_out, register_3_q, register_7_q;

  and and_1 (and_1_out, MEM_MemWrite, 1'b1);
  and and_2 (and_2_out, MEM_MemRead, 1'b1);
  and and_3 (and_3_out, MEM_Branch, 1'b1);
  and and_4 (and_4_out, WB_MemtoReg, 1'b1);
  and and_5 (and_5_out, WB_RegWrite, 1'b1);
  Register #(.width(1), .trigger("falling")) register_1 (
    .D(and_1_out), .Q(MEM_MemWrite_2), .clk(Clock));  // open: en, clr
  Register #(.width(1), .trigger("falling")) register_2 (
    .D(and_2_out), .Q(MEM_MemRead_2), .clk(Clock));  // open: en, clr
  Register #(.width(1), .trigger("falling")) register_3 (
    .D(and_3_out), .Q(register_3_q), .clk(Clock));  // open: en, clr
  Register #(.width(1), .trigger("falling")) register_4 (
    .D(and_4_out), .Q(WB_MemtoReg_2), .clk(Clock));  // open: en, clr
  Register #(.width(1), .trigger("falling")) register_5 (
    .D(and_5_out), .Q(WB_RegWrite_2), .clk(Clock));  // open: en, clr
  Register #(.trigger("falling")) register_6 (.D(Adder_Result), .Q(Adder_Result_2), .clk(Clock));  // open: en, clr
  Register #(.width(1), .trigger("falling")) register_7 (.D(Zero_ALU), .Q(register_7_q), .clk(Clock));  // open: en, clr
  Register #(.width(16), .trigger("falling")) register_8 (
    .D(Result_ALU), .Q(Result_ALU_2), .clk(Clock));  // open: en, clr
  Register #(.width(16), .trigger("falling")) register_9 (
    .D(ReadData2), .Q(ReadData2_2), .clk(Clock));  // open: en, clr
  Register #(.width(3), .trigger("falling")) register_10 (
    .D(WriteRegister_RS), .Q(WriteRegister_RS_2), .clk(Clock));  // open: en, clr
  and and_6 (PCSource, register_3_q, register_7_q);
endmodule

module Mem_WB_Buffer (
  input  WB_MemtoReg,
  input  WB_RegWrite,
  input  [15:0] Data,
  input  [15:0] Result_ALU,
  input  [2:0] WriteRegister,
  input  Bubble,
  input  Clock,
  output WB_MemtoReg_2,
  output WB_RegWrite_2,
  output [15:0] Data_2,
  output [15:0] Result_ALU_2,
  output [2:0] WriteRegister_2
);

  wire and_1_out, and_2_out;

  and and_1 (and_1_out, WB_MemtoReg, 1'b1);
  and and_2 (and_2_out, WB_RegWrite, 1'b1);
  Register #(.width(1), .trigger("falling")) register_1 (
    .D(and_1_out), .Q(WB_MemtoReg_2), .clk(Clock));  // open: en, clr
  Register #(.width(1), .trigger("falling")) register_2 (
    .D(and_2_out), .Q(WB_RegWrite_2), .clk(Clock));  // open: en, clr
  Register #(.width(16), .trigger("falling")) register_3 (.D(Data), .Q(Data_2), .clk(Clock));  // open: en, clr
  Register #(.width(16), .trigger("falling")) register_4 (.D(Result_ALU), .Q(Result_ALU_2));  // open: en, clk, clr
  Register #(.width(3), .trigger("falling")) register_5 (
    .D(WriteRegister), .Q(WriteRegister_2), .clk(Clock));  // open: en, clr
endmodule

module ALU_Adder (
  input  [7:0] PC,
  input  [15:0] IMM_ext,
  output [7:0] AdderResult
);

  wire [7:0] bit_extender_1_out, shifter_1_out;

  Bit_Extender #(.in_width(16), .out_width(8)) bit_extender_1 (.in(IMM_ext), .out(bit_extender_1_out));
  Shifter_part shifter_1 (.in(bit_extender_1_out), .\dist (3'b001), .out(shifter_1_out));
  Adder adder_1 (.a(PC), .b(shifter_1_out), .out(AdderResult));  // open: cin, cout
endmodule

module TestCircuit (
  input  [7:0] PC,
  output [3:0] ALUOp
);

  wire button_1_out, clock_1_out;
  wire [7:0] register_1_q;
  wire [11:0] rom_1_data;

  Clock clock_1 (.out(clock_1_out));
  Register register_1 (.D(PC), .Q(register_1_q), .clk(clock_1_out), .clr(button_1_out));  // open: en
  Button button_1 (.out(button_1_out));
  ROM #(.dataWidth(16)) rom_1 (
    .addr(register_1_q), .data({ALUOp[0], ALUOp[1], ALUOp[2], ALUOp[3], rom_1_data}));  // open: sel

  // Notes on the sheet:
  //   contents of rom_1 (hex, n*v repeats v):
  //   1203 0 0 0 1204 1405 440 f400
endmodule

// ForwardUnit
module FU (
  input  [2:0] RS_EX,
  input  [2:0] RS_Mem,
  input  RegisterWrite_Mem,
  input  [2:0] RS_WB,
  input  RegisterWrite_WB,
  input  [2:0] RT_EX,
  output [1:0] MuxAEn,
  output [1:0] MuxBEn
);

  wire comparator_1_eq, comparator_2_eq, comparator_3_eq, comparator_4_eq, comparator_5_eq, comparator_6_eq,
       not_1_out, not_2_out, not_3_out;

  Comparator #(.width(3)) comparator_1 (.a(RS_EX), .b(3'b000), .eq(comparator_1_eq));  // open: gt, lt
  Comparator #(.width(3)) comparator_2 (.a(RS_EX), .b(RS_Mem), .eq(comparator_2_eq));  // open: gt, lt
  not not_1 (not_1_out, comparator_3_eq);
  Comparator #(.width(3)) comparator_3 (.a(RS_EX), .b(RS_WB), .eq(comparator_3_eq));  // open: gt, lt
  not not_2 (not_2_out, comparator_1_eq);
  and MEM_A (MuxAEn[1], not_2_out, comparator_2_eq, RegisterWrite_Mem);
  and WB_A (MuxAEn[0], not_2_out, not_1_out, RegisterWrite_WB);
  and WB_B (MuxBEn[0], comparator_5_eq, comparator_4_eq, RegisterWrite_WB);
  and MEM_B (MuxBEn[1], comparator_5_eq, RegisterWrite_Mem, not_3_out);
  Comparator #(.width(3)) comparator_4 (.a(RS_WB), .b(RT_EX), .eq(comparator_4_eq));  // open: gt, lt
  Comparator #(.width(3)) comparator_5 (.a(RS_Mem), .b(RT_EX), .eq(comparator_5_eq));  // open: gt, lt
  Comparator #(.width(3)) comparator_6 (.a(3'b000), .b(RT_EX), .eq(comparator_6_eq));  // open: gt, lt
  not not_3 (not_3_out, comparator_6_eq);
endmodule
